# Fritzing sketch boosted (saved by Fritzing 0.9.2b)
breadboards: 1

parts:
  Teensy1 = Teensy 3.6 (Basic)
  Q1 = npn-Powertransistor [package="TO220 [THT]"]
  Polar = Basic Servo
  D1 = Rectifier Diode [part_number=1N4001 package="300 mil [THT]"]  # not connected
  Q2 = npn-Powertransistor [package="TO220 [THT]"]
  Azimuth = Basic Servo
  D2 = Rectifier Diode [part_number=1N4001 package="300 mil [THT]"]  # not connected
  Q3 = npn-Powertransistor [package="TO220 [THT]"]
  Left_Trigger = Basic Servo
  D3 = Rectifier Diode [part_number=1N4001 package="300 mil [THT]"]  # not connected
  Q4 = npn-Powertransistor [package="TO220 [THT]"]
  eRight_Triggert = Basic Servo
  D4 = Rectifier Diode [part_number=1N4001 package="300 mil [THT]"]  # not connected

nets:
  N1: Teensy1.A6/D20, Q4.base
  N2: Teensy1.A7/D21, Q3.base
  N3: Teensy1.A8/D22, Q2.base
  N4: Teensy1.A9/D23, Q1.base
  N5: Q1.emitter, Polar.gnd
  5V: Polar.pulse, Azimuth.pulse, Left_Trigger.pulse, eRight_Triggert.pulse
  N6: Q2.emitter, Azimuth.gnd
  N7: Q3.emitter, Left_Trigger.gnd
  N8: Q4.emitter, eRight_Triggert.gnd

custom parts:
  Teensy 3.6 (Basic): The Teensy is a complete USB-based microcontoller development system, in a very small footprint, capable of implementing many types of projects. All programming is done via the USB port. No special programmer is needed, only a standard micro-USB cable and a PC or Macintosh with a USB port.
