# Fritzing sketch dual (saved by Fritzing 0.9.2b)
breadboards: 1

parts:
  Teensy1 = Teensy 3.6 (Basic)
  Part1 = Arduino Uno (Rev3) - ICSP
  J1 = Basic Servo
  J2 = Basic Servo
  Azimuth1 = Basic Servo
  Polar1 = Basic Servo

nets:
  GND: Teensy1.GND, Teensy1.GND1, Part1.GND, J1.gnd, J2.gnd, Azimuth1.gnd, Polar1.gnd
  N1: Teensy1.A8/D22, Azimuth1.pulse
  N2: Teensy1.A9/D23, Polar1.pulse
  N3: Part1.A0, J2.pulse
  N4: Part1.A1, J1.pulse
  VCC: Part1.5V, J1.vcc, J2.vcc, Azimuth1.vcc, Polar1.vcc

custom parts:
  Teensy 3.6 (Basic): The Teensy is a complete USB-based microcontoller development system, in a very small footprint, capable of implementing many types of projects. All programming is done via the USB port. No special programmer is needed, only a standard micro-USB cable and a PC or Macintosh with a USB port.
